// Logisim project F6.circ as structural Verilog: 9 circuits, main circuit main
module main (
  input  in_1,
  input  in_2,
  output [31:0] out_3
);

  wire clock_1_out, module_decode_1_is_addi, module_decode_1_is_imm;
  wire [4:0] module_decode_1_rd, module_decode_1_rs1;
  wire [6:0] module_decode_1_opcode;
  wire [9:0] module_splitter_1_out0;
  wire [11:0] module_decode_1_imm_raw;
  wire [31:0] module_adder_1_out0, module_alu_1_out0, module_bit_extender_1_out0,
       module_register_file_1_out0, rom_1_data;

  Clock clock_1 (.out(clock_1_out));
  Module_PC module_pc_1 (.In0(module_adder_1_out0), .We(in_1), .Clk(clock_1_out), .Reset(in_2), .Out0(out_3));
  Module_adder module_adder_1 (.In0(out_3), .Out0(module_adder_1_out0));
  Module_Splitter module_splitter_1 (.In0(out_3), .Out0(module_splitter_1_out0));
  ROM #(.addrWidth(10), .dataWidth(32)) rom_1 (.addr(module_splitter_1_out0), .data(rom_1_data));
  Module_Decode module_decode_1 (
    .In0(rom_1_data), .Is_Addi(module_decode_1_is_addi), .is_imm(module_decode_1_is_imm),
    .Opcode(module_decode_1_opcode), .Rd(module_decode_1_rd), .Rs1(module_decode_1_rs1),
    .imm_raw(module_decode_1_imm_raw));  // open: Funct3
  Module_Bit_Extender module_bit_extender_1 (.In0(module_decode_1_imm_raw), .Out0(module_bit_extender_1_out0));
  Module_Register_File module_register_file_1 (
    .Is_Addi(module_decode_1_is_addi), .Is_Jalr(module_decode_1_is_imm), .Sel_Decoder(module_decode_1_rd),
    .Clk(clock_1_out), .Reset(in_2), .Mux_Sel(module_decode_1_rs1), .Out0(module_register_file_1_out0));  // open: Write_Data
  Module_Alu module_alu_1 (
    .In0(module_register_file_1_out0), .In1(module_bit_extender_1_out0), .Out0(module_alu_1_out0));

  // Notes on the sheet:
  //   contents of rom_1 (hex, n*v repeats v):
  //   1400513 10000e7 fff00293
endmodule

module Module_adder (
  input  [31:0] In0,
  output [31:0] Out0
);

  Adder #(.width(32)) adder_1 (.a(32'h4), .b(In0), .out(Out0));  // open: cin, cout
endmodule

module Module_PC (
  input  [31:0] In0,
  input  We,
  input  Clk,
  input  Reset,
  output [31:0] Out0
);

  Register #(.width(32)) Pc (.D(In0), .en(We), .clk(Clk), .Q(Out0), .clr(Reset));
endmodule

module Module_Splitter (
  input  [31:0] In0,
  output [9:0] Out0
);


  assign Out0 = In0[11:2];
endmodule

module Module_Rom (
  input  [9:0] In0,
  output [31:0] Out0
);

  ROM #(.addrWidth(10), .dataWidth(32)) rom_1 (.addr(In0), .data(Out0));
endmodule

module Module_Decode (
  input  [31:0] In0,
  output Is_Addi,
  output [6:0] Opcode,
  output [4:0] Rd,
  output is_imm,
  output [2:0] Funct3,
  output [4:0] Rs1,
  output [11:0] imm_raw
);

  Comparator #(.width(7)) comparator_1 (.a(In0[6:0]), .b(7'b0010011), .eq(Is_Addi));  // open: gt, lt
  Comparator #(.width(7)) comparator_2 (.a(In0[6:0]), .b(7'b1100111), .eq(is_imm));  // open: gt, lt

  assign Funct3 = In0[14:12];
  assign imm_raw = In0[31:20];
  assign Opcode = In0[6:0];
  assign Rd = In0[11:7];
  assign Rs1 = In0[19:15];
endmodule

module Module_Alu (
  input  [31:0] In0,
  input  [31:0] In1,
  output [31:0] Out0
);

  Adder #(.width(32)) adder_1 (.a(In0), .b(In1), .out(Out0));  // open: cin, cout
endmodule

module Module_Bit_Extender (
  input  [11:0] In0,
  output [31:0] Out0
);

  assign Out0 = {{20{In0[11]}}, In0};  // Bit_Extender bit_extender_1
endmodule

module Module_Register_File (
  input  Is_Addi,
  input  Is_Jalr,
  input  [4:0] Sel_Decoder,
  input  [31:0] Write_Data,
  input  Clk,
  input  Reset,
  input  [4:0] Mux_Sel,
  output [31:0] Out0
);

  wire decoder_1_out1, decoder_1_out2, decoder_1_out3, decoder_1_out4, decoder_1_out5, decoder_1_out6,
       decoder_1_out7, decoder_1_out8, decoder_1_out9, decoder_1_out10, decoder_1_out11, decoder_1_out12,
       decoder_1_out13, decoder_1_out14, decoder_1_out15, decoder_1_out16, decoder_1_out17, decoder_1_out18,
       decoder_1_out19, decoder_1_out20, decoder_1_out21, decoder_1_out22, decoder_1_out23, decoder_1_out24,
       decoder_1_out25, decoder_1_out26, decoder_1_out27, decoder_1_out28, decoder_1_out29, decoder_1_out30,
       decoder_1_out31, or_1_out;
  wire [31:0] x0_q, x1_q, x2_q, x3_q, x4_q, x5_q, x6_q, x7_q, x8_q, x9_q, x10_q, x11_q, x12_q, x13_q, x14_q,
       x15_q, x16_q, x17_q, x18_q, x19_q, x20_q, x21_q, x22_q, x23_q, x24_q, x25_q, x26_q, x27_q, x28_q,
       x29_q, x30_q, x31_q;

  or or_1 (or_1_out, Is_Addi, Is_Jalr);
  Decoder #(.select(5)) decoder_1 (
    .out1(decoder_1_out1), .out2(decoder_1_out2), .out3(decoder_1_out3), .out4(decoder_1_out4),
    .out5(decoder_1_out5), .out6(decoder_1_out6), .out7(decoder_1_out7), .out8(decoder_1_out8),
    .out9(decoder_1_out9), .out10(decoder_1_out10), .out11(decoder_1_out11), .out12(decoder_1_out12),
    .out13(decoder_1_out13), .out14(decoder_1_out14), .out15(decoder_1_out15), .out16(decoder_1_out16),
    .out17(decoder_1_out17), .out18(decoder_1_out18), .out19(decoder_1_out19), .out20(decoder_1_out20),
    .out21(decoder_1_out21), .out22(decoder_1_out22), .out23(decoder_1_out23), .out24(decoder_1_out24),
    .out25(decoder_1_out25), .out26(decoder_1_out26), .out27(decoder_1_out27), .out28(decoder_1_out28),
    .out29(decoder_1_out29), .out30(decoder_1_out30), .out31(decoder_1_out31), .sel(Sel_Decoder),
    .en(or_1_out));  // open: out0
  Register #(.width(32)) x0 (.D(Write_Data), .en(1'b0), .clk(Clk), .Q(x0_q), .clr(Reset));
  Register #(.width(32)) x8 (.D(Write_Data), .en(decoder_1_out8), .clk(Clk), .Q(x8_q), .clr(Reset));
  Register #(.width(32)) x16 (.D(Write_Data), .en(decoder_1_out16), .clk(Clk), .Q(x16_q), .clr(Reset));
  Register #(.width(32)) x24 (.D(Write_Data), .en(decoder_1_out24), .clk(Clk), .Q(x24_q), .clr(Reset));
  Register #(.width(32)) x1 (.D(Write_Data), .en(decoder_1_out1), .clk(Clk), .Q(x1_q), .clr(Reset));
  Register #(.width(32)) x9 (.D(Write_Data), .en(decoder_1_out9), .clk(Clk), .Q(x9_q), .clr(Reset));
  Register #(.width(32)) x17 (.D(Write_Data), .en(decoder_1_out17), .clk(Clk), .Q(x17_q), .clr(Reset));
  Register #(.width(32)) x25 (.D(Write_Data), .en(decoder_1_out25), .clk(Clk), .Q(x25_q), .clr(Reset));
  Register #(.width(32)) x2 (.D(Write_Data), .en(decoder_1_out2), .clk(Clk), .Q(x2_q), .clr(Reset));
  Register #(.width(32)) x10 (.D(Write_Data), .en(decoder_1_out10), .clk(Clk), .Q(x10_q), .clr(Reset));
  Register #(.width(32)) x18 (.D(Write_Data), .en(decoder_1_out18), .clk(Clk), .Q(x18_q), .clr(Reset));
  Register #(.width(32)) x26 (.D(Write_Data), .en(decoder_1_out26), .clk(Clk), .Q(x26_q), .clr(Reset));
  Register #(.width(32)) x3 (.D(Write_Data), .en(decoder_1_out3), .clk(Clk), .Q(x3_q), .clr(Reset));
  Register #(.width(32)) x11 (.D(Write_Data), .en(decoder_1_out11), .clk(Clk), .Q(x11_q), .clr(Reset));
  Register #(.width(32)) x19 (.D(Write_Data), .en(decoder_1_out19), .clk(Clk), .Q(x19_q), .clr(Reset));
  Register #(.width(32)) x27 (.D(Write_Data), .en(decoder_1_out27), .clk(Clk), .Q(x27_q), .clr(Reset));
  Register #(.width(32)) x4 (.D(Write_Data), .en(decoder_1_out4), .clk(Clk), .Q(x4_q), .clr(Reset));
  Register #(.width(32)) x12 (.D(Write_Data), .en(decoder_1_out12), .clk(Clk), .Q(x12_q), .clr(Reset));
  Register #(.width(32)) x20 (.D(Write_Data), .en(decoder_1_out20), .clk(Clk), .Q(x20_q), .clr(Reset));
  Register #(.width(32)) x28 (.D(Write_Data), .en(decoder_1_out28), .clk(Clk), .Q(x28_q), .clr(Reset));
  Register #(.width(32)) x5 (.D(Write_Data), .en(decoder_1_out5), .clk(Clk), .Q(x5_q), .clr(Reset));
  Register #(.width(32)) x13 (.D(Write_Data), .en(decoder_1_out13), .clk(Clk), .Q(x13_q), .clr(Reset));
  Register #(.width(32)) x21 (.D(Write_Data), .en(decoder_1_out21), .clk(Clk), .Q(x21_q), .clr(Reset));
  Register #(.width(32)) x29 (.D(Write_Data), .en(decoder_1_out29), .clk(Clk), .Q(x29_q), .clr(Reset));
  Register #(.width(32)) x6 (.D(Write_Data), .en(decoder_1_out6), .clk(Clk), .Q(x6_q), .clr(Reset));
  Register #(.width(32)) x14 (.D(Write_Data), .en(decoder_1_out14), .clk(Clk), .Q(x14_q), .clr(Reset));
  Register #(.width(32)) x22 (.D(Write_Data), .en(decoder_1_out22), .clk(Clk), .Q(x22_q), .clr(Reset));
  Register #(.width(32)) x30 (.D(Write_Data), .en(decoder_1_out30), .clk(Clk), .Q(x30_q), .clr(Reset));
  Register #(.width(32)) x7 (.D(Write_Data), .en(decoder_1_out7), .clk(Clk), .Q(x7_q), .clr(Reset));
  Register #(.width(32)) x15 (.D(Write_Data), .en(decoder_1_out15), .clk(Clk), .Q(x15_q), .clr(Reset));
  Register #(.width(32)) x23 (.D(Write_Data), .en(decoder_1_out23), .clk(Clk), .Q(x23_q), .clr(Reset));
  Register #(.width(32)) x31 (.D(Write_Data), .en(decoder_1_out31), .clk(Clk), .Q(x31_q), .clr(Reset));
  Multiplexer #(.select(5), .width(32)) multiplexer_1 (
    .in0(x0_q), .in1(x1_q), .in2(x2_q), .in3(x3_q), .in4(x4_q), .in5(x5_q), .in6(x6_q), .in7(x7_q),
    .in8(x8_q), .in9(x9_q), .in10(x10_q), .in11(x11_q), .in12(x12_q), .in13(x13_q), .in14(x14_q),
    .in15(x15_q), .in16(x16_q), .in17(x17_q), .in18(x18_q), .in19(x19_q), .in20(x20_q), .in21(x21_q),
    .in22(x22_q), .in23(x23_q), .in24(x24_q), .in25(x25_q), .in26(x26_q), .in27(x27_q), .in28(x28_q),
    .in29(x29_q), .in30(x30_q), .in31(x31_q), .out(Out0), .sel(Mux_Sel));
endmodule
