// Logisim project F6.circ as structural Verilog: 17 circuits, main circuit main
module main (
  input  in_1,
  input  in_2
);

  wire clock_1_out, module_byte_enable_decoder_1_out0, module_byte_enable_decoder_1_out1,
       module_byte_enable_decoder_1_out2, module_byte_enable_decoder_1_out3, module_decode_1_is_add,
       module_decode_1_is_addi, module_decode_1_is_imm, module_decode_1_is_lbu, module_decode_1_is_lui,
       module_decode_1_is_lw, module_decode_1_is_sb, module_decode_1_is_sw, or_1_out, or_2_out, or_3_out,
       or_4_out, or_5_out;
  wire [1:0] module_alu_1_byte_sel;
  wire [4:0] module_decode_1_rd, module_decode_1_rs1, module_decode_1_rs2;
  wire [19:0] module_splitter_1_out0;
  wire [31:0] module_adder_1_out0, module_alu_1_out0, module_alu_input_mux_1_mux_out,
       module_decode_1_imm_i_ext, module_decode_1_imm_s_ext, module_decode_1_imm_u, module_load_mux_1_out0,
       module_pc_1_out0, module_ram_1_read_data, module_ram_mux_1_out0, module_ram_output_splitter_1_out0,
       module_register_file_1_rs1_data, module_register_file_1_rs2_data, module_write_back_mux0_1_mux_out,
       multiplexer_1_out, rom_1_data;

  Clock clock_1 (.out(clock_1_out));
  Module_PC module_pc_1 (.In0(multiplexer_1_out), .We(in_1), .Clk(clock_1_out), .Reset(in_2), .Out0(module_pc_1_out0));
  Module_adder module_adder_1 (.In0(module_pc_1_out0), .Out0(module_adder_1_out0));
  Multiplexer #(.width(32)) multiplexer_1 (
    .in0(module_adder_1_out0), .in1(module_alu_1_out0), .out(multiplexer_1_out), .sel(module_decode_1_is_imm));
  Module_Splitter module_splitter_1 (.In0(module_pc_1_out0), .Out0(module_splitter_1_out0));
  ROM #(.addrWidth(20), .dataWidth(32)) rom_1 (.addr(module_splitter_1_out0), .data(rom_1_data));
  Module_Decode module_decode_1 (
    .In0(rom_1_data), .Is_Addi(module_decode_1_is_addi), .Rd(module_decode_1_rd),
    .is_imm(module_decode_1_is_imm), .Rs1(module_decode_1_rs1), .imm_i_ext(module_decode_1_imm_i_ext),
    .Rs2(module_decode_1_rs2), .imm_u(module_decode_1_imm_u), .Is_Add(module_decode_1_is_add),
    .Is_Lui(module_decode_1_is_lui), .Is_Lw(module_decode_1_is_lw), .Is_Sw(module_decode_1_is_sw),
    .imm_s_ext(module_decode_1_imm_s_ext), .Is_Lbu(module_decode_1_is_lbu), .Is_Sb(module_decode_1_is_sb));  // open: Opcode, Funct3
  or or_1 (or_1_out, module_decode_1_is_sb, module_decode_1_is_sw);
  Module_Register_File module_register_file_1 (
    .Is_Addi(module_decode_1_is_addi), .Is_Jalr(module_decode_1_is_imm), .Is_Add(module_decode_1_is_add),
    .Is_Lui(module_decode_1_is_lui), .Is_Lw(module_decode_1_is_lw), .Sel_Decoder(module_decode_1_rd),
    .Write_Data(module_write_back_mux0_1_mux_out), .Clk(clock_1_out), .Reset(in_2),
    .Mux1_Sel(module_decode_1_rs2), .Mux0_Sel(module_decode_1_rs1), .Is_Lbu(module_decode_1_is_lbu),
    .Rs2_Data(module_register_file_1_rs2_data), .Rs1_Data(module_register_file_1_rs1_data));
  Module_Alu_Input_Mux module_alu_input_mux_1 (
    .In0(module_decode_1_imm_i_ext), .In1(module_register_file_1_rs2_data), .In2(module_decode_1_imm_s_ext),
    .Is_Add(module_decode_1_is_add), .Is_Sw(module_decode_1_is_sw), .Is_Sb(module_decode_1_is_sb),
    .Mux_Out(module_alu_input_mux_1_mux_out));  // open: In3
  Module_Ram_Mux module_ram_mux_1 (
    .In0(module_register_file_1_rs2_data), .Is_Sb(module_decode_1_is_sb), .Out0(module_ram_mux_1_out0));
  Module_Alu module_alu_1 (
    .In0(module_register_file_1_rs1_data), .In1(module_alu_input_mux_1_mux_out), .Out0(module_alu_1_out0),
    .Byte_Sel(module_alu_1_byte_sel));
  Module_Write_Back_Mux0 module_write_back_mux0_1 (
    .In0(module_alu_1_out0), .In1(module_adder_1_out0), .In2(module_decode_1_imm_u),
    .In3(module_load_mux_1_out0), .Is_Lui(module_decode_1_is_lui), .Is_Jalr(module_decode_1_is_imm),
    .Is_Lw(module_decode_1_is_lw), .Is_Lbu(module_decode_1_is_lbu), .Mux_Out(module_write_back_mux0_1_mux_out));
  Module_Ram module_ram_1 (
    .A(module_alu_1_out0), .WE(or_1_out), .OE(1'b1), .BE0(or_2_out), .BE1(or_3_out), .BE2(or_4_out),
    .BE3(or_5_out), .Clk(clock_1_out), .Write_Data(module_ram_mux_1_out0), .Read_Data(module_ram_1_read_data));
  Module_Ram_Output_Splitter module_ram_output_splitter_1 (
    .In0(module_ram_1_read_data), .Byte_Sel(module_alu_1_byte_sel), .Out0(module_ram_output_splitter_1_out0));
  Module_Byte_Enable_Decoder module_byte_enable_decoder_1 (
    .Byte_Sel(module_alu_1_byte_sel), .Is_Sb(module_decode_1_is_sb),
    .Out0(module_byte_enable_decoder_1_out0), .Out1(module_byte_enable_decoder_1_out1),
    .Out2(module_byte_enable_decoder_1_out2), .Out3(module_byte_enable_decoder_1_out3));
  or or_2 (or_2_out, module_byte_enable_decoder_1_out0, module_decode_1_is_sw);
  or or_3 (or_3_out, module_byte_enable_decoder_1_out1, module_decode_1_is_sw);
  or or_4 (or_4_out, module_byte_enable_decoder_1_out2, module_decode_1_is_sw);
  or or_5 (or_5_out, module_byte_enable_decoder_1_out3, module_decode_1_is_sw);
  Module_Load_Mux module_load_mux_1 (
    .In_lw(module_ram_1_read_data), .In_lbu(module_ram_output_splitter_1_out0),
    .Is_Lbu(module_decode_1_is_lbu), .Out0(module_load_mux_1_out0));

  // Notes on the sheet:
  //   contents of rom_1 (hex, n*v repeats v):
  //   413 51137 10113 22c00093 80e7 fea12823 fe812e23 40800413 ff014183 3401b3 1c183 ff114203 440233 24203
  //   4181b3 ff214203 440233 24203 4181b3 ff314203 440233 24203 4181b3 40000213 320233 24203 ffc12403
  //   420233 420233 410233 9400193 fe312823 9000193 fe312623 fec22203 20067 8067 ff410113 100513 112423
  //   22400093 80e7 ff010113 112623 12023 100793 6500693 12703 f70733 e12023 178793 fef12823 fed12623
  //   fe812e23 fe912c23 30000413 ff014183 340233 100193 320023 fec14183 3401b3 18023 24183 ff114483 940233
  //   100493 920023 fed14483 9404b3 48023 24483 9181b3 ff214483 940233 100493 920023 fee14483 9404b3 48023
  //   24483 9181b3 ff314483 940233 100493 920023 fef14483 9404b3 48023 24483 9181b3 40000213 320233 24203
  //   ff812483 ffc12403 420233 420233 410233 1a400193 fe312823 bc00193 fe312623 fec22203 20067 12503
  //   fffff7b7 c4678793 f50533 fea12823 fe812e23 40800413 ff014183 3401b3 1c183 ff114203 440233 24203
  //   4181b3 ff214203 440233 24203 4181b3 ff314203 440233 24203 4181b3 40000213 320233 24503 ffc12403
  //   1400093 80e7 c12083 513 1010113 8067 22400213 20067 ff410113 48537 60050513 112423 a800093 80e7
  //   22400093 80e7 109*0 1 0 1010100 63*1010101 100 1000101 1010100 1000000 1010100 121*0 64*1000100
  //   64*2020000 64*3020100 0 4040404 0 4040404 0 4040404 0 4040404 0 4040404 0 4040404 0 4040404 0
  //   4040404 0 4040404 0 4040404 0 4040404 0 4040404 0 4040404 0 4040404 0 4040404 0 4040404 0 4040404 0
  //   4040404 0 4040404 0 4040404 0 4040404 0 4040404 0 4040404 0 4040404 0 4040404 0 4040404 0 4040404 0
  //   4040404 0 4040404 0 4040404 0 4040404 0 4040404 1000100 5040504 1000100 5040504 1000100 5040504
  //   1000100 5040504 1000100 5040504 1000100 5040504 1000100 5040504 1000100 5040504 1000100 5040504
  //   1000100 5040504 1000100 5040504 1000100 5040504 1000100 5040504 1000100 5040504 1000100 5040504
  //   1000100 5040504 1000100 5040504 1000100 5040504 1000100 5040504 1000100 5040504 1000100 5040504
  //   1000100 5040504 1000100 5040504 1000100 5040504 1000100 5040504 1000100 5040504 1000100 5040504
  //   1000100 5040504 1000100 5040504 1000100 5040504 1000100 5040504 1000100 5040504 2020000 6060404
  //   2020000 6060404 2020000 6060404 2020000 6060404 2020000 6060404 2020000 6060404 2020000 6060404
  //   2020000 6060404 2020000 6060404 2020000 6060404 2020000 6060404 2020000 6060404 2020000 6060404
  //   2020000 6060404 2020000 6060404 2020000 6060404 2020000 6060404 2020000 6060404 2020000 6060404
  //   2020000 6060404 2020000 6060404 2020000 6060404 2020000 6060404 2020000 6060404 2020000 6060404
  //   2020000 6060404 2020000 6060404 2020000 6060404 2020000 6060404 2020000 6060404 2020000 6060404
  //   2020000 6060404 3020100 7060504 3020100 7060504 3020100 7060504 3020100 7060504 3020100 7060504
  //   3020100 7060504 3020100 7060504 3020100 7060504 3020100 7060504 3020100 7060504 3020100 7060504
  //   3020100 7060504 3020100 7060504 3020100 7060504 3020100 7060504 3020100 7060504 3020100 7060504
  //   3020100 7060504 3020100 7060504 3020100 7060504 3020100 7060504 3020100 7060504 3020100 7060504
  //   3020100 7060504 3020100 7060504 3020100 7060504 3020100 7060504 3020100 7060504 3020100 7060504
  //   3020100 7060504 3020100 7060504 3020100 7060504 0 0 8080808 8080808 0 0 8080808 8080808 0 0 8080808
  //   8080808 0 0 8080808 8080808 0 0 8080808 8080808 0 0 8080808 8080808 0 0 8080808 8080808 0 0 8080808
  //   8080808 0 0 8080808 8080808 0 0 8080808 8080808 0 0 8080808 8080808 0 0 8080808 8080808 0 0 8080808
  //   8080808 0 0 8080808 8080808 0 0 8080808 8080808 0 0 8080808 8080808 1000100 1000100 9080908 9080908
  //   1000100 1000100 9080908 9080908 1000100 1000100 9080908 9080908 1000100 1000100 9080908 9080908
  //   1000100 1000100 9080908 9080908 1000100 1000100 9080908 9080908 1000100 1000100 9080908 9080908
  //   1000100 1000100 9080908 9080908 1000100 1000100 9080908 9080908 1000100 1000100 9080908 9080908
  //   1000100 1000100 9080908 9080908 1000100 1000100 9080908 9080908 1000100 1000100 9080908 9080908
  //   1000100 1000100 9080908 9080908 1000100 1000100 9080908 9080908 1000100 1000100 9080908 9080908
  //   2020000 2020000 a0a0808 a0a0808 2020000 2020000 a0a0808 a0a0808 2020000 2020000 a0a0808 a0a0808
  //   2020000 2020000 a0a080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
endmodule

module Module_adder (
  input  [31:0] In0,
  output [31:0] Out0
);

  Adder #(.width(32)) adder_1 (.a(32'h4), .b(In0), .out(Out0));  // open: cin, cout
endmodule

module Module_Register_File (
  input  Is_Addi,
  input  Is_Jalr,
  input  Is_Add,
  input  Is_Lui,
  input  Is_Lw,
  input  [4:0] Sel_Decoder,
  input  [31:0] Write_Data,
  input  Clk,
  input  Reset,
  input  [4:0] Mux1_Sel,
  input  [4:0] Mux0_Sel,
  input  Is_Lbu,
  output [31:0] Rs2_Data,
  output [31:0] Rs1_Data
);

  wire decoder_1_out1, decoder_1_out2, decoder_1_out3, decoder_1_out4, decoder_1_out5, decoder_1_out6,
       decoder_1_out7, decoder_1_out8, decoder_1_out9, decoder_1_out10, decoder_1_out11, decoder_1_out12,
       decoder_1_out13, decoder_1_out14, decoder_1_out15, decoder_1_out16, decoder_1_out17, decoder_1_out18,
       decoder_1_out19, decoder_1_out20, decoder_1_out21, decoder_1_out22, decoder_1_out23, decoder_1_out24,
       decoder_1_out25, decoder_1_out26, decoder_1_out27, decoder_1_out28, decoder_1_out29, decoder_1_out30,
       decoder_1_out31, or_1_out;
  wire [31:0] x0_q, x1_q, x2_q, x3_q, x4_q, x5_q, x6_q, x7_q, x8_q, x9_q, x10_q, x11_q, x12_q, x13_q, x14_q,
       x15_q, x16_q, x17_q, x18_q, x19_q, x20_q, x21_q, x22_q, x23_q, x24_q, x25_q, x26_q, x27_q, x28_q,
       x29_q, x30_q, x31_q;

  or or_1 (or_1_out, Is_Addi, Is_Jalr, Is_Add, Is_Lui, Is_Lw, Is_Lbu);
  Decoder #(.select(5)) decoder_1 (
    .out1(decoder_1_out1), .out2(decoder_1_out2), .out3(decoder_1_out3), .out4(decoder_1_out4),
    .out5(decoder_1_out5), .out6(decoder_1_out6), .out7(decoder_1_out7), .out8(decoder_1_out8),
    .out9(decoder_1_out9), .out10(decoder_1_out10), .out11(decoder_1_out11), .out12(decoder_1_out12),
    .out13(decoder_1_out13), .out14(decoder_1_out14), .out15(decoder_1_out15), .out16(decoder_1_out16),
    .out17(decoder_1_out17), .out18(decoder_1_out18), .out19(decoder_1_out19), .out20(decoder_1_out20),
    .out21(decoder_1_out21), .out22(decoder_1_out22), .out23(decoder_1_out23), .out24(decoder_1_out24),
    .out25(decoder_1_out25), .out26(decoder_1_out26), .out27(decoder_1_out27), .out28(decoder_1_out28),
    .out29(decoder_1_out29), .out30(decoder_1_out30), .out31(decoder_1_out31), .sel(Sel_Decoder),
    .en(or_1_out));  // open: out0
  Register #(.width(32)) x0 (.D(Write_Data), .en(1'b0), .clk(Clk), .Q(x0_q), .clr(Reset));
  Register #(.width(32)) x8 (.D(Write_Data), .en(decoder_1_out8), .clk(Clk), .Q(x8_q), .clr(Reset));
  Register #(.width(32)) x16 (.D(Write_Data), .en(decoder_1_out16), .clk(Clk), .Q(x16_q), .clr(Reset));
  Register #(.width(32)) x24 (.D(Write_Data), .en(decoder_1_out24), .clk(Clk), .Q(x24_q), .clr(Reset));
  Register #(.width(32)) x1 (.D(Write_Data), .en(decoder_1_out1), .clk(Clk), .Q(x1_q), .clr(Reset));
  Register #(.width(32)) x9 (.D(Write_Data), .en(decoder_1_out9), .clk(Clk), .Q(x9_q), .clr(Reset));
  Register #(.width(32)) x17 (.D(Write_Data), .en(decoder_1_out17), .clk(Clk), .Q(x17_q), .clr(Reset));
  Register #(.width(32)) x25 (.D(Write_Data), .en(decoder_1_out25), .clk(Clk), .Q(x25_q), .clr(Reset));
  Register #(.width(32)) x2 (.D(Write_Data), .en(decoder_1_out2), .clk(Clk), .Q(x2_q), .clr(Reset));
  Register #(.width(32)) x10 (.D(Write_Data), .en(decoder_1_out10), .clk(Clk), .Q(x10_q), .clr(Reset));
  Register #(.width(32)) x18 (.D(Write_Data), .en(decoder_1_out18), .clk(Clk), .Q(x18_q), .clr(Reset));
  Register #(.width(32)) x26 (.D(Write_Data), .en(decoder_1_out26), .clk(Clk), .Q(x26_q), .clr(Reset));
  Register #(.width(32)) x3 (.D(Write_Data), .en(decoder_1_out3), .clk(Clk), .Q(x3_q), .clr(Reset));
  Register #(.width(32)) x11 (.D(Write_Data), .en(decoder_1_out11), .clk(Clk), .Q(x11_q), .clr(Reset));
  Register #(.width(32)) x19 (.D(Write_Data), .en(decoder_1_out19), .clk(Clk), .Q(x19_q), .clr(Reset));
  Register #(.width(32)) x27 (.D(Write_Data), .en(decoder_1_out27), .clk(Clk), .Q(x27_q), .clr(Reset));
  Register #(.width(32)) x4 (.D(Write_Data), .en(decoder_1_out4), .clk(Clk), .Q(x4_q), .clr(Reset));
  Register #(.width(32)) x12 (.D(Write_Data), .en(decoder_1_out12), .clk(Clk), .Q(x12_q), .clr(Reset));
  Register #(.width(32)) x20 (.D(Write_Data), .en(decoder_1_out20), .clk(Clk), .Q(x20_q), .clr(Reset));
  Register #(.width(32)) x28 (.D(Write_Data), .en(decoder_1_out28), .clk(Clk), .Q(x28_q), .clr(Reset));
  Register #(.width(32)) x5 (.D(Write_Data), .en(decoder_1_out5), .clk(Clk), .Q(x5_q), .clr(Reset));
  Register #(.width(32)) x13 (.D(Write_Data), .en(decoder_1_out13), .clk(Clk), .Q(x13_q), .clr(Reset));
  Register #(.width(32)) x21 (.D(Write_Data), .en(decoder_1_out21), .clk(Clk), .Q(x21_q), .clr(Reset));
  Register #(.width(32)) x29 (.D(Write_Data), .en(decoder_1_out29), .clk(Clk), .Q(x29_q), .clr(Reset));
  Register #(.width(32)) x6 (.D(Write_Data), .en(decoder_1_out6), .clk(Clk), .Q(x6_q), .clr(Reset));
  Register #(.width(32)) x14 (.D(Write_Data), .en(decoder_1_out14), .clk(Clk), .Q(x14_q), .clr(Reset));
  Register #(.width(32)) x22 (.D(Write_Data), .en(decoder_1_out22), .clk(Clk), .Q(x22_q), .clr(Reset));
  Register #(.width(32)) x30 (.D(Write_Data), .en(decoder_1_out30), .clk(Clk), .Q(x30_q), .clr(Reset));
  Register #(.width(32)) x7 (.D(Write_Data), .en(decoder_1_out7), .clk(Clk), .Q(x7_q), .clr(Reset));
  Register #(.width(32)) x15 (.D(Write_Data), .en(decoder_1_out15), .clk(Clk), .Q(x15_q), .clr(Reset));
  Register #(.width(32)) x23 (.D(Write_Data), .en(decoder_1_out23), .clk(Clk), .Q(x23_q), .clr(Reset));
  Register #(.width(32)) x31 (.D(Write_Data), .en(decoder_1_out31), .clk(Clk), .Q(x31_q), .clr(Reset));
  Multiplexer #(.select(5), .width(32)) multiplexer_1 (
    .in0(x0_q), .in1(x1_q), .in2(x2_q), .in3(x3_q), .in4(x4_q), .in5(x5_q), .in6(x6_q), .in7(x7_q),
    .in8(x8_q), .in9(x9_q), .in10(x10_q), .in11(x11_q), .in12(x12_q), .in13(x13_q), .in14(x14_q),
    .in15(x15_q), .in16(x16_q), .in17(x17_q), .in18(x18_q), .in19(x19_q), .in20(x20_q), .in21(x21_q),
    .in22(x22_q), .in23(x23_q), .in24(x24_q), .in25(x25_q), .in26(x26_q), .in27(x27_q), .in28(x28_q),
    .in29(x29_q), .in30(x30_q), .in31(x31_q), .out(Rs1_Data), .sel(Mux0_Sel));
  Multiplexer #(.select(5), .width(32)) multiplexer_2 (
    .in0(x0_q), .in1(x1_q), .in2(x2_q), .in3(x3_q), .in4(x4_q), .in5(x5_q), .in6(x6_q), .in7(x7_q),
    .in8(x8_q), .in9(x9_q), .in10(x10_q), .in11(x11_q), .in12(x12_q), .in13(x13_q), .in14(x14_q),
    .in15(x15_q), .in16(x16_q), .in17(x17_q), .in18(x18_q), .in19(x19_q), .in20(x20_q), .in21(x21_q),
    .in22(x22_q), .in23(x23_q), .in24(x24_q), .in25(x25_q), .in26(x26_q), .in27(x27_q), .in28(x28_q),
    .in29(x29_q), .in30(x30_q), .in31(x31_q), .out(Rs2_Data), .sel(Mux1_Sel));
endmodule

module Module_PC (
  input  [31:0] In0,
  input  We,
  input  Clk,
  input  Reset,
  output [31:0] Out0
);

  Register #(.width(32)) Pc (.D(In0), .en(We), .clk(Clk), .Q(Out0), .clr(Reset));
endmodule

module Module_Splitter (
  input  [31:0] In0,
  output [19:0] Out0
);


  assign Out0 = In0[21:2];
endmodule

module Module_Rom (
  input  [9:0] In0,
  output [31:0] Out0
);

  ROM #(.addrWidth(10), .dataWidth(32)) rom_1 (.addr(In0), .data(Out0));
endmodule

module Module_Bit_Extender (
  output [31:0] Out0
);

  wire [11:0] undriven;

  assign Out0 = {{20{undriven[11]}}, undriven};  // Bit_Extender bit_extender_1
endmodule

module Module_Decode (
  input  [31:0] In0,
  output Is_Addi,
  output [6:0] Opcode,
  output [4:0] Rd,
  output is_imm,
  output [2:0] Funct3,
  output [4:0] Rs1,
  output [31:0] imm_i_ext,
  output [4:0] Rs2,
  output [31:0] imm_u,
  output Is_Add,
  output Is_Lui,
  output Is_Lw,
  output Is_Sw,
  output [31:0] imm_s_ext,
  output Is_Lbu,
  output Is_Sb
);

  wire comparator_3_eq, comparator_6_eq, comparator_7_eq, comparator_8_eq, comparator_9_eq;

  assign imm_s_ext = {{20{In0[31]}}, {In0[31:25], In0[11:7]}};  // Bit_Extender bit_extender_1
  Comparator #(.width(7)) comparator_1 (.a(In0[6:0]), .b(7'b0010011), .eq(Is_Addi));  // open: gt, lt
  Comparator #(.width(7)) comparator_2 (.a(In0[6:0]), .b(7'b1100111), .eq(is_imm));  // open: gt, lt
  assign imm_i_ext = {{20{In0[31]}}, In0[31:20]};  // Bit_Extender bit_extender_2
  Comparator #(.width(3)) comparator_3 (.a(In0[14:12]), .b(3'b100), .eq(comparator_3_eq));  // open: gt, lt
  Comparator #(.width(7)) comparator_4 (.a(In0[6:0]), .b(7'b0110011), .eq(Is_Add));  // open: gt, lt
  Comparator #(.width(7)) comparator_5 (.a(In0[6:0]), .b(7'b0110111), .eq(Is_Lui));  // open: gt, lt
  Comparator #(.width(7)) comparator_6 (.a(In0[6:0]), .b(7'b0000011), .eq(comparator_6_eq));  // open: gt, lt
  Comparator #(.width(3)) comparator_7 (.a(In0[14:12]), .b(3'b010), .eq(comparator_7_eq));  // open: gt, lt
  Comparator #(.width(7)) comparator_8 (.a(In0[6:0]), .b(7'b0100011), .eq(comparator_8_eq));  // open: gt, lt
  and and_1 (Is_Lw, comparator_6_eq, comparator_7_eq);
  and and_2 (Is_Sw, comparator_8_eq, comparator_7_eq);
  Comparator #(.width(3)) comparator_9 (.a(In0[14:12]), .b(3'b000), .eq(comparator_9_eq));  // open: gt, lt
  and and_3 (Is_Sb, comparator_9_eq, comparator_8_eq);
  and and_4 (Is_Lbu, comparator_6_eq, comparator_3_eq);

  assign Funct3 = In0[14:12];
  assign imm_u = {In0[31:12], {12{1'b0}}};
  assign Opcode = In0[6:0];
  assign Rd = In0[11:7];
  assign Rs1 = In0[19:15];
  assign Rs2 = In0[24:20];
endmodule

module Module_is_Lui (
  input  [6:0] In0,
  output Out0
);

  Comparator #(.width(7)) comparator_1 (.a(In0), .b(7'b0110111), .eq(Out0));  // open: gt, lt
endmodule

module Module_Ram (
  input  [31:0] A,
  input  WE,
  input  OE,
  input  BE0,
  input  BE1,
  input  BE2,
  input  BE3,
  input  Clk,
  input  [31:0] Write_Data,
  output [31:0] Read_Data
);

  RAM #(.addrWidth(20), .asyncread("true"), .byteenables("byteEnables"), .dataWidth(32), .\type ("nonvolatile")) ram_1 (
    .addr(A[21:2]), .we(WE), .oe(OE), .clk(Clk), .din(Write_Data), .dout(Read_Data), .be3(BE3), .be2(BE2),
    .be1(BE1), .be0(BE0));
endmodule

module Module_Write_Back_Mux0 (
  input  [31:0] In0,
  input  [31:0] In1,
  input  [31:0] In2,
  input  [31:0] In3,
  input  Is_Lui,
  input  Is_Jalr,
  input  Is_Lw,
  input  Is_Lbu,
  output [31:0] Mux_Out
);

  wire [1:0] or_1_out;

  Multiplexer #(.select(2), .width(32)) multiplexer_1 (
    .in0(In0), .in1(In1), .in2(In2), .in3(In3), .out(Mux_Out), .sel(or_1_out));
  or or_1 (or_1_out[0], Is_Jalr, Is_Lbu, Is_Lw);
  or or_2 (or_1_out[1], Is_Lui, Is_Lbu, Is_Lw);
endmodule

module Module_Alu_Input_Mux (
  input  [31:0] In0,
  input  [31:0] In1,
  input  [31:0] In2,
  input  [31:0] In3,
  input  Is_Add,
  input  Is_Sw,
  input  Is_Sb,
  output [31:0] Mux_Out
);

  wire [1:1] or_1_out;

  or or_1 (or_1_out[1], Is_Sw, Is_Sb);
  Multiplexer #(.select(2), .width(32)) multiplexer_1 (
    .in0(In0), .in1(In1), .in2(In2), .in3(In3), .out(Mux_Out), .sel({or_1_out[1], Is_Add}));
endmodule

module Module_Byte_Enable_Decoder (
  input  [1:0] Byte_Sel,
  input  Is_Sb,
  output Out0,
  output Out1,
  output Out2,
  output Out3
);

  Decoder #(.select(2)) decoder_1 (.out0(Out0), .out1(Out1), .out2(Out2), .out3(Out3), .sel(Byte_Sel), .en(Is_Sb));
endmodule

module Module_Alu (
  input  [31:0] In0,
  input  [31:0] In1,
  output [31:0] Out0,
  output [1:0] Byte_Sel
);

  Adder #(.width(32)) adder_1 (.a(In0), .b(In1), .out({Out0[31:2], Byte_Sel}));  // open: cin, cout

  assign Out0[1:0] = Byte_Sel;
endmodule

module Module_Ram_Mux (
  input  [31:0] In0,
  input  Is_Sb,
  output [31:0] Out0
);

  Multiplexer #(.width(32)) multiplexer_1 (
    .in0(In0), .in1({In0[7:0], In0[7:0], In0[7:0], In0[7:0]}), .out(Out0), .sel(Is_Sb));
endmodule

module Module_Ram_Output_Splitter (
  input  [31:0] In0,
  input  [1:0] Byte_Sel,
  output [31:0] Out0
);

  wire [7:0] multiplexer_1_out;

  Multiplexer #(.select(2), .width(8)) multiplexer_1 (
    .in0(In0[7:0]), .in1(In0[15:8]), .in2(In0[23:16]), .in3(In0[31:24]), .out(multiplexer_1_out),
    .sel(Byte_Sel));
  assign Out0 = {{24{1'b0}}, multiplexer_1_out};  // Bit_Extender bit_extender_1
endmodule

module Module_Load_Mux (
  input  [31:0] In_lw,
  input  [31:0] In_lbu,
  input  Is_Lbu,
  output [31:0] Out0
);

  Multiplexer #(.width(32)) multiplexer_1 (.in0(In_lw), .in1(In_lbu), .out(Out0), .sel(Is_Lbu));
endmodule
